// Logisim project Termostat_centrala_termica.circ as structural Verilog
module main (
  input  [4:0] in_1,
  output [5:0] out_2,
  output [5:0] out_3,
  output [4:0] out_4,
  output out_5,
  output out_6,
  output [4:0] out_7
);

  wire clock_1_out, comparator_2_nr_1_egale, numarator_minute_1_schimba_ora,
       numarator_secunde_1_schimba_minutul;
  wire [3:0] binary_to_decimal_converter_1_decimal, binary_to_decimal_converter_1_unit,
       binary_to_decimal_converter_2_decimal, binary_to_decimal_converter_2_unit,
       binary_to_decimal_converter_5_biti_1_decimal, binary_to_decimal_converter_5_biti_1_unit,
       binary_to_decimal_converter_5_biti_2_decimal, binary_to_decimal_converter_5_biti_2_unit;
  wire [4:0] mux_8_la1_1_temp_aleasa, undriven;
  wire [6:0] bcd_1_segment, bcd_2_segment, bcd_3_segment, bcd_4_segment, bcd_5_segment, bcd_6_segment,
       bcd_7_segment, bcd_8_segment;

  Clock clock_1 (.out(clock_1_out));
  Numarator_secunde numarator_secunde_1 (
    .clock(clock_1_out), .timp(out_2), .schimba_minutul(numarator_secunde_1_schimba_minutul));
  Numarator_minute numarator_minute_1 (
    .enable(numarator_secunde_1_schimba_minutul), .clock(clock_1_out), .timp(out_3),
    .schimba_ora(numarator_minute_1_schimba_ora));
  Numarator_ore numarator_ore_1 (.enable(numarator_minute_1_schimba_ora), .clock(clock_1_out), .timp(out_7));
  Binary_to_decimal_converter binary_to_decimal_converter_1 (
    .Bin_num(out_2), .Unit(binary_to_decimal_converter_1_unit),
    .Decimal(binary_to_decimal_converter_1_decimal));
  comparator_2_nr comparator_2_nr_1 (.a(out_4), .b(in_1), .egale(comparator_2_nr_1_egale));
  mux_8_la1 mux_8_la1_1 (
    .temp_initiala(in_1), .temp_modificata(out_4), .sel(comparator_2_nr_1_egale),
    .temp_aleasa(mux_8_la1_1_temp_aleasa));
  Binary_to_decimal_converter_5_biti binary_to_decimal_converter_5_biti_1 (
    .Bin_num(out_7), .Unit(binary_to_decimal_converter_5_biti_1_unit),
    .Decimal(binary_to_decimal_converter_5_biti_1_decimal));
  bcd bcd_1 (.number(binary_to_decimal_converter_1_unit), .segment(bcd_1_segment));
  bcd bcd_2 (.number(binary_to_decimal_converter_1_decimal), .segment(bcd_2_segment));
  _7_Segment_Display u_7_segment_display_1 (
    .g(bcd_2_segment[0]), .f(bcd_2_segment[1]), .a(bcd_2_segment[6]), .b(bcd_2_segment[5]),
    .e(bcd_2_segment[2]), .d(bcd_2_segment[3]), .c(bcd_2_segment[4]));  // open: dp
  termostat termostat_1 (
    .clock(clock_1_out), .ora(out_7), .temperatura_actuala(mux_8_la1_1_temp_aleasa),
    .temperatura_finala(out_4), .incalzire(out_5), .racire(out_6));
  Binary_to_decimal_converter binary_to_decimal_converter_2 (
    .Bin_num(out_3), .Unit(binary_to_decimal_converter_2_unit),
    .Decimal(binary_to_decimal_converter_2_decimal));
  bcd bcd_3 (.number(binary_to_decimal_converter_5_biti_1_unit), .segment(bcd_3_segment));
  bcd bcd_4 (.number(binary_to_decimal_converter_5_biti_1_decimal), .segment(bcd_4_segment));
  bcd bcd_5 (.number(binary_to_decimal_converter_2_decimal), .segment(bcd_5_segment));
  _7_Segment_Display u_7_segment_display_2 (
    .g(bcd_4_segment[0]), .f(bcd_4_segment[1]), .a(bcd_4_segment[6]), .b(bcd_4_segment[5]),
    .e(bcd_4_segment[2]), .d(bcd_4_segment[3]), .c(bcd_4_segment[4]));  // open: dp
  _7_Segment_Display u_7_segment_display_3 (
    .g(bcd_1_segment[0]), .f(bcd_1_segment[1]), .a(bcd_1_segment[6]), .b(bcd_1_segment[5]),
    .e(bcd_1_segment[2]), .d(bcd_1_segment[3]), .c(bcd_1_segment[4]));  // open: dp
  _7_Segment_Display u_7_segment_display_4 (
    .g(bcd_5_segment[0]), .f(bcd_5_segment[1]), .a(bcd_5_segment[6]), .b(bcd_5_segment[5]),
    .e(bcd_5_segment[2]), .d(bcd_5_segment[3]), .c(bcd_5_segment[4]));  // open: dp
  bcd bcd_6 (.number(binary_to_decimal_converter_2_unit), .segment(bcd_6_segment));
  _7_Segment_Display u_7_segment_display_5 (
    .g(bcd_3_segment[0]), .f(bcd_3_segment[1]), .a(bcd_3_segment[6]), .b(bcd_3_segment[5]),
    .e(bcd_3_segment[2]), .d(bcd_3_segment[3]), .c(bcd_3_segment[4]));  // open: dp
  _7_Segment_Display u_7_segment_display_6 (
    .g(bcd_6_segment[0]), .f(bcd_6_segment[1]), .a(bcd_6_segment[6]), .b(bcd_6_segment[5]),
    .e(bcd_6_segment[2]), .d(bcd_6_segment[3]), .c(bcd_6_segment[4]));  // open: dp
  Binary_to_decimal_converter_5_biti binary_to_decimal_converter_5_biti_2 (
    .Bin_num(undriven), .Unit(binary_to_decimal_converter_5_biti_2_unit),
    .Decimal(binary_to_decimal_converter_5_biti_2_decimal));
  bcd bcd_7 (.number(binary_to_decimal_converter_5_biti_2_unit), .segment(bcd_7_segment));
  bcd bcd_8 (.number(binary_to_decimal_converter_5_biti_2_decimal), .segment(bcd_8_segment));
  _7_Segment_Display u_7_segment_display_7 (
    .g(bcd_8_segment[0]), .f(bcd_8_segment[1]), .a(bcd_8_segment[6]), .b(bcd_8_segment[5]),
    .e(bcd_8_segment[2]), .d(bcd_8_segment[3]), .c(bcd_8_segment[4]));  // open: dp
  _7_Segment_Display u_7_segment_display_8 (
    .g(bcd_7_segment[0]), .f(bcd_7_segment[1]), .a(bcd_7_segment[6]), .b(bcd_7_segment[5]),
    .e(bcd_7_segment[2]), .d(bcd_7_segment[3]), .c(bcd_7_segment[4]));  // open: dp
endmodule

// VHDL entity Numarator_secunde, as the project stores it:
LIBRARY ieee;
USE ieee.std_logic_1164.all;
USE ieee.std_logic_UNSIGNED.all;

ENTITY Numarator_secunde IS
  PORT (
  		clock: IN std_logic;
  		timp: OUT std_logic_vector(5 downto 0);
  		schimba_minutul: OUT std_logic
    );
END Numarator_secunde;

--------------------------------------------------------------------------------
--Complete your VHDL description below
--------------------------------------------------------------------------------

ARCHITECTURE TypeArchitecture OF Numarator_secunde IS

BEGIN
Process(clock)
Variable tmp: std_logic_vector(5 downto 0):= "000000";
Begin
	if(rising_edge(clock)) then
		if(tmp="111010") then
			tmp:="000000";
			schimba_minutul<='1';
		else
			tmp:=tmp+'1';
			schimba_minutul<='0';
		end if;
	end if;
	timp<=tmp;
End Process;
			

END TypeArchitecture;

// VHDL entity Numarator_minute, as the project stores it:
LIBRARY ieee;
USE ieee.std_logic_1164.all;
USE ieee.std_logic_UNSIGNED.all;

ENTITY Numarator_minute IS
  PORT (
  		enable: IN std_logic;
  		clock: IN std_logic;
  		timp: OUT std_logic_vector(5 downto 0);
  		schimba_ora: OUT std_logic
    );
END Numarator_minute;

--------------------------------------------------------------------------------
--Complete your VHDL description below
--------------------------------------------------------------------------------

ARCHITECTURE TypeArchitecture OF Numarator_minute IS

BEGIN

Process(clock)
Variable tmp: std_logic_vector(5 downto 0):= "000000";
Begin
	if(rising_edge(clock) and enable='1') then
		if(tmp="111010") then
			tmp:="000000";
			schimba_ora<='1';
		else
			tmp:=tmp+'1';
			schimba_ora<='0';
		end if;
	end if;
	timp<=tmp;
End Process;
			

END TypeArchitecture;

// VHDL entity Numarator_ore, as the project stores it:
LIBRARY ieee;
USE ieee.std_logic_1164.all;
USE ieee.std_logic_UNSIGNED.all;

ENTITY Numarator_ore IS
  PORT (
  		enable: IN std_logic;
  		clock: IN std_logic;
  		timp: OUT std_logic_vector(4 downto 0)
    );
END Numarator_ore;

--------------------------------------------------------------------------------
--Complete your VHDL description below
--------------------------------------------------------------------------------

ARCHITECTURE TypeArchitecture OF Numarator_ore IS

BEGIN

Process(clock)
Variable tmp: std_logic_vector(4 downto 0):= "00000";
Begin
	if(rising_edge(clock) and enable='1') then
		if(tmp="10111") then
			tmp:="00000";
		else
			tmp:=tmp+'1';
		end if;
	end if;
	timp<=tmp;
End Process;
			

END TypeArchitecture;

// VHDL entity termostat, as the project stores it:
LIBRARY ieee;
USE ieee.std_logic_1164.all;
use IEEE.numeric_std.all;
USE ieee.std_logic_UNSIGNED.all;

ENTITY termostat IS
  PORT (
  	clock: IN std_logic;
  	ora: IN std_logic_vector(4 downto 0);
  	temperatura_actuala: IN std_logic_vector(4 downto 0);
  	temperatura_finala: OUT std_logic_vector(4 downto 0);
  	incalzire: OUT std_logic;
  	racire: OUT std_logic
  );
END termostat;

--------------------------------------------------------------------------------
--Complete your VHDL description below
--------------------------------------------------------------------------------

ARCHITECTURE TypeArchitecture OF termostat IS
	signal ora_baza10: integer;
	type tabel is array (0 to 23) of std_logic_vector(4 downto 0);
	constant temp_min: tabel:= ("10000","10000","10000","10000","10000","10000","10000","10000","10000","10000","10000","10000","10000","10000","10000","10000","10000","10000","10000","10000","10000","10000","10000","10000");
	constant temp_max: tabel:= ("10110","10110","10110","10110","10110","10110","10110","10110","10110","10110","10110","10110","10110","10110","10110","10110","10110","10110","10110","10110","10110","10110","10110","10110");
BEGIN
ora_baza10 <= to_integer(unsigned(ora));	
process(clock)
variable temperatura_auxiliara: std_logic_vector(4 downto 0):="01001";
begin
temperatura_finala <= "01001";
     if(rising_edge(clock)) then 
	if(temperatura_actuala < temp_min(ora_baza10)) then
		temperatura_auxiliara := temperatura_actuala+'1';
		incalzire <='1';
		racire <= '0';
	elsif(temperatura_actuala>temp_max(ora_baza10)) then
		temperatura_auxiliara := temperatura_actuala-'1';
		incalzire <='0';
		racire <= '1';
	else incalzire <= '0';
		racire <= '0';
	end if;
	end if;
	temperatura_finala <= temperatura_auxiliara;
End process;

END TypeArchitecture;

// VHDL entity mux_8_la1, as the project stores it:
LIBRARY ieee;
USE ieee.std_logic_1164.all;

ENTITY mux_8_la1 IS
  PORT (
  		temp_initiala: IN std_logic_vector(4 downto 0);
  		temp_modificata: IN std_logic_vector(4 downto 0);
  		sel: IN std_logic;
  		temp_aleasa: OUT std_logic_vector(4 downto 0)
  );
END mux_8_la1;


ARCHITECTURE TypeArchitecture OF mux_8_la1 IS

BEGIN
	with sel select temp_aleasa<= temp_initiala when '1',
							temp_modificata when others;

END TypeArchitecture;

// VHDL entity comparator_2_nr, as the project stores it:
LIBRARY ieee;
USE ieee.std_logic_1164.all;

ENTITY comparator_2_nr IS
  PORT (
  	a,b:in std_logic_vector(4 downto 0);
  	egale:out std_logic
  );
END comparator_2_nr;


ARCHITECTURE TypeArchitecture OF comparator_2_nr IS

BEGIN
egale <= (a(4) and b(4)) and (a(3) and b(3)) and (a(2) and b(2)) and (a(1) and b(1)) and (a(0) and b(0));

END TypeArchitecture;

// VHDL entity Binary_to_decimal_converter, as the project stores it:
--------------------------------------------------------------------------------
-- Project :
-- File    :
-- Autor   :
-- Date    :
--
--------------------------------------------------------------------------------
-- Description :
--
--------------------------------------------------------------------------------

LIBRARY ieee;
USE ieee.std_logic_1164.all;
USE ieee.std_logic_unsigned.all;
USE ieee.std_logic_arith.all;

ENTITY Binary_to_decimal_converter IS
  PORT (
 Bin_num: in std_logic_vector(5 downto 0);
  		Unit: out std_logic_vector(3 downto 0);
  		Decimal: out std_logic_vector(3 downto 0)  
    );
END Binary_to_decimal_converter;

--------------------------------------------------------------------------------
--Complete your VHDL description below
--------------------------------------------------------------------------------

ARCHITECTURE comport OF Binary_to_decimal_converter IS

signal num_int: integer:=0;
signal u,z: integer:=0;
BEGIN

	num_int<=conv_integer(bin_num);
	z<=num_int / 10;
	u<=num_int rem 10;
	process(u)
	begin
		case u is
		when 0 => unit <= x"0";
		when 1 => unit <= x"1";
		when 2 => unit <= x"2";
		when 3 => unit <= x"3";
		when 4 => unit <= x"4";
		when 5 => unit <= x"5";
		when 6 => unit <= x"6";
		when 7 => unit <= x"7";
		when 8 => unit <= x"8";
		when 9 => unit <= x"9";
		when others => unit <=x"f";
		end case;
	end process;
	process(z)
	begin
		case z is
		when 0 => Decimal <= x"0";
		when 1 => Decimal <= x"1";
		when 2 => Decimal <= x"2";
		when 3 => Decimal <= x"3";
		when 4 => Decimal <= x"4";
		when 5 => Decimal <= x"5";
		when 6 => Decimal <= x"6";
		when 7 => Decimal <= x"7";
		when 8 => Decimal <= x"8";
		when 9 => Decimal <= x"9";
		when others => Decimal <=x"f";
		end case;
	end process;
		 

	
END comport;

// VHDL entity bcd, as the project stores it:
--------------------------------------------------------------------------------
-- Project :
-- File    :
-- Autor   :
-- Date    :
--
--------------------------------------------------------------------------------
-- Description :
--
--------------------------------------------------------------------------------

LIBRARY ieee;
USE ieee.std_logic_1164.all;

ENTITY bcd IS
  PORT (
  number: in std_logic_vector(3 downto 0);
  segment: out std_logic_vector(6 downto 0)
    );
END bcd;

--------------------------------------------------------------------------------
--Complete your VHDL description below
--------------------------------------------------------------------------------

ARCHITECTURE TypeArchitecture OF bcd IS

signal aux:std_logic_vector (6 downto 0);
BEGIN

with number select
 aux <=
 "1111110" when x"0",
 "0110000" when x"1",
 "1101101" when x"2",
 "1111001" when x"3",
 "0110011" when x"4",
 "1011011" when x"5",
 "1011111" when x"6",
 "1110000" when x"7",
 "1111111" when x"8",
 "1111011" when x"9",
 "0000000" when others;
segment <= aux;

END TypeArchitecture;

// VHDL entity Binary_to_decimal_converter_5_biti, as the project stores it:
--------------------------------------------------------------------------------
-- Project :
-- File    :
-- Autor   :
-- Date    :
--
--------------------------------------------------------------------------------
-- Description :
--
--------------------------------------------------------------------------------

LIBRARY ieee;
USE ieee.std_logic_1164.all;
USE ieee.std_logic_unsigned.all;
USE ieee.std_logic_arith.all;

ENTITY Binary_to_decimal_converter_5_biti IS
  PORT (
 Bin_num: in std_logic_vector(4 downto 0);
  		Unit: out std_logic_vector(3 downto 0);
  		Decimal: out std_logic_vector(3 downto 0)  
    );
END Binary_to_decimal_converter_5_biti;

--------------------------------------------------------------------------------
--Complete your VHDL description below
--------------------------------------------------------------------------------

ARCHITECTURE comport OF Binary_to_decimal_converter_5_biti IS

signal num_int: integer:=0;
signal u,z: integer:=0;
BEGIN

	num_int<=conv_integer(bin_num);
	z<=num_int / 10;
	u<=num_int rem 10;
	process(u)
	begin
		case u is
		when 0 => unit <= x"0";
		when 1 => unit <= x"1";
		when 2 => unit <= x"2";
		when 3 => unit <= x"3";
		when 4 => unit <= x"4";
		when 5 => unit <= x"5";
		when 6 => unit <= x"6";
		when 7 => unit <= x"7";
		when 8 => unit <= x"8";
		when 9 => unit <= x"9";
		when others => unit <=x"f";
		end case;
	end process;
	process(z)
	begin
		case z is
		when 0 => Decimal <= x"0";
		when 1 => Decimal <= x"1";
		when 2 => Decimal <= x"2";
		when 3 => Decimal <= x"3";
		when 4 => Decimal <= x"4";
		when 5 => Decimal <= x"5";
		when 6 => Decimal <= x"6";
		when 7 => Decimal <= x"7";
		when 8 => Decimal <= x"8";
		when 9 => Decimal <= x"9";
		when others => Decimal <=x"f";
		end case;
	end process;
		 

	
END comport;

// VHDL entity Freq_Divider, as the project stores it:
LIBRARY ieee;
USE ieee.std_logic_1164.all;

ENTITY Freq_Divider IS
 --divides from 100 MHz to 1 Hz; 100 MHz = 100.000.000 Hz
  PORT (
  
	clock: IN std_logic;
  	divided_clock: OUT std_logic
    );
END Freq_Divider;

ARCHITECTURE TypeArchitecture OF Freq_Divider IS

signal count: INTEGER := 1;
signal newClock: std_logic;

BEGIN
divided_clock <= newClock;
process(clock)
begin
	if(rising_edge(clock)) then
		if count<49999999 then 
		  count<=count +1;
		elsif count = 49999999 then
		  count <= 0;
	      newClock <= not newClock;
	    end if;
	end if;
		
end process;

END TypeArchitecture;
